// Logisim project 4bitAdderSubtractor.circ as structural Verilog: 1 circuit, main circuit main
module main (
  input  A,
  input  B,
  input  Cin,
  input  K,
  input  in_5,
  input  [3:0] in_6,
  input  [3:0] in_7,
  input  in_8,
  input  in_9,
  input  in_10,
  input  in_11,
  input  in_12,
  input  in_13,
  input  in_14,
  input  in_15,
  output Y,
  output Cout,
  output out_18,
  output out_19,
  output out_20,
  output out_21,
  output out_22,
  output [3:0] out_23,
  output Cout_2
);

  wire a_out, adder_1_cout, adder_2_cout, adder_3_cout, and_1_out, and_2_out, and_3_out, and_4_out,
       and_5_out, and_6_out, and_7_out, and_8_out, b_out, d_out, e_out, f_out, or_2_out, or_3_out, xor_1_out,
       xor_2_out, xor_3_out, xor_4_out, xor_5_out, xor_7_out, xor_8_out, xor_9_out, xor_11_out, xor_12_out,
       xor_14_out;

  xor xor_1 (xor_1_out, in_9, in_5);
  xor xor_2 (xor_2_out, in_11, in_5);
  xor xor_3 (xor_3_out, in_13, in_5);
  xor xor_4 (xor_4_out, in_15, in_5);
  xor xor_5 (xor_5_out, A, B);
  and and_1 (and_1_out, A, B);
  xor xor_6 (Y, xor_5_out, Cin);
  buf and_2 (and_2_out, Cin);  // AND_Gate
  or or_1 (Cout, and_2_out, and_1_out);
  Adder #(.width(1)) adder_1 (.a(in_8), .b(xor_1_out), .out(out_18), .cin(in_5), .cout(adder_1_cout));
  Adder #(.width(1)) adder_2 (.a(in_10), .b(xor_2_out), .out(out_19), .cin(adder_1_cout), .cout(adder_2_cout));
  Adder #(.width(1)) adder_3 (.a(in_12), .b(xor_3_out), .out(out_20), .cin(adder_2_cout), .cout(adder_3_cout));
  Adder #(.width(1)) adder_4 (.a(in_14), .b(xor_4_out), .out(out_21), .cin(adder_3_cout), .cout(out_22));
  xor u_a (a_out, in_7[0], K);
  xor u_b (b_out, in_6[0], a_out);
  and d (d_out, in_6[0], a_out);
  xor xor_7 (xor_7_out, in_7[1], K);
  xor c (out_23[0], b_out, K);
  and e (e_out, b_out, K);
  or f (f_out, e_out, d_out);
  xor xor_8 (xor_8_out, in_6[1], xor_7_out);
  and and_3 (and_3_out, in_6[1], xor_7_out);
  xor xor_9 (xor_9_out, in_7[2], K);
  xor xor_10 (out_23[1], xor_8_out, f_out);
  and and_4 (and_4_out, xor_8_out, f_out);
  and and_5 (and_5_out, in_6[2], xor_9_out);
  or or_2 (or_2_out, and_4_out, and_3_out);
  xor xor_11 (xor_11_out, in_6[2], xor_9_out);
  xor xor_12 (xor_12_out, in_7[3], K);
  xor xor_13 (out_23[2], xor_11_out, or_2_out);
  and and_6 (and_6_out, xor_11_out, or_2_out);
  or or_3 (or_3_out, and_6_out, and_5_out);
  xor xor_14 (xor_14_out, in_6[3], xor_12_out);
  and and_7 (and_7_out, in_6[3], xor_12_out);
  and and_8 (and_8_out, xor_14_out, or_3_out);
  xor xor_15 (out_23[3], xor_14_out, or_3_out);
  or or_4 (Cout_2, and_8_out, and_7_out);

  // Notes on the sheet:
  //   simple version
  //   Full adder
  //   A
  //   B
  //   4 bit Adder subtracter
  //   Y
endmodule
