// Logisim project simple4bitRegister.circ as structural Verilog: 1 circuit, main circuit main
module main (
  input  in_1,
  input  [3:0] in_2,
  input  in_3,
  input  in_4
);

  wire d_ff_1_q, d_ff_2_q, d_ff_3_q, d_ff_4_q;
  wire [3:0] controlled_buffer_1_out;

  D_Flip_Flop d_ff_1 (.D(controlled_buffer_1_out[0]), .clk(in_3), .Q(d_ff_1_q));  // open: Qn, preset, reset
  D_Flip_Flop d_ff_2 (.D(controlled_buffer_1_out[1]), .clk(in_3), .Q(d_ff_2_q));  // open: Qn, preset, reset
  assign controlled_buffer_1_out[0] = in_4 ? d_ff_1_q : 1'bz;  // Controlled_Buffer controlled_buffer_1
  D_Flip_Flop d_ff_3 (.D(controlled_buffer_1_out[2]), .clk(in_3), .Q(d_ff_3_q));  // open: Qn, preset, reset
  assign controlled_buffer_1_out[1] = in_4 ? d_ff_2_q : 1'bz;  // Controlled_Buffer controlled_buffer_2
  D_Flip_Flop d_ff_4 (.D(controlled_buffer_1_out[3]), .clk(in_3), .Q(d_ff_4_q));  // open: Qn, preset, reset
  assign controlled_buffer_1_out[2] = in_4 ? d_ff_3_q : 1'bz;  // Controlled_Buffer controlled_buffer_3
  assign controlled_buffer_1_out[3] = in_4 ? d_ff_4_q : 1'bz;  // Controlled_Buffer controlled_buffer_4
  assign controlled_buffer_1_out = in_1 ? in_2 : 4'bz;  // Controlled_Buffer controlled_buffer_5
endmodule
