// Logisim project volledig.circ as structural Verilog: 1 circuit, main circuit main
module main (
  input  [7:0] in_1,
  input  in_2,
  input  [7:0] in_3,
  input  [7:0] in_4,
  input  [7:0] in_5,
  input  [7:0] in_6,
  input  [7:0] in_7,
  input  [7:0] in_8,
  input  [7:0] in_9,
  input  [7:0] in_10,
  input  [7:0] in_11,
  input  [7:0] in_12,
  input  [7:0] in_13,
  input  [7:0] in_14,
  input  [7:0] in_15,
  input  [7:0] in_16,
  input  [7:0] in_17,
  output [3:0] out_18
);

  wire adder_1_cout, adder_2_cout, adder_3_cout, and_1_out, and_2_out, and_3_out, and_5_out, clock_1_out,
       controlled_buffer_1_out, controlled_buffer_2_out, controlled_buffer_3_out, controlled_buffer_4_out,
       controlled_buffer_15_out, controlled_buffer_16_out, controlled_buffer_17_out,
       controlled_buffer_18_out, controlled_inverter_1_out, d_ff_21_q, decoder_1_out1, decoder_1_out2,
       decoder_1_out3, decoder_3_out0, decoder_3_out1, decoder_3_out2, decoder_3_out3, nor_1_out, not_1_out,
       subtractor_1_bout, subtractor_2_bout, subtractor_3_bout, xor_1_out, xor_2_out, xor_3_out, xor_4_out;
  wire [1:0] controlled_buffer_10_out, controlled_buffer_12_out, controlled_buffer_14_out;
  wire [3:0] adder_1_out, and_6_out, controlled_buffer_19_out, d_ff_1_q, d_ff_5_q, d_ff_6_q, d_ff_7_q,
       decoder_2_out0, decoder_4_out0, multiplexer_2_out, multiplexer_3_out, multiplexer_4_out,
       subtractor_1_out, xor_5_out;
  wire [7:0] multiplexer_1_out;

  and and_1 (and_1_out, in_2, d_ff_1_q[0]);
  and and_2 (and_2_out, and_1_out, d_ff_1_q[1]);
  and and_3 (and_3_out, and_2_out, d_ff_1_q[2]);
  // AND_Gate and_4 has open pins: in0=and_3_out, in1=d_ff_1_q[3], out=open
  xor xor_1 (xor_1_out, d_ff_1_q[1], and_1_out);
  xor xor_2 (xor_2_out, d_ff_1_q[2], and_2_out);
  xor xor_3 (xor_3_out, d_ff_1_q[3], and_3_out);
  xor xor_4 (xor_4_out, d_ff_1_q[0], in_2);
  assign controlled_buffer_1_out = not_1_out ? xor_4_out : 1'bz;  // Controlled_Buffer controlled_buffer_1
  assign controlled_buffer_2_out = not_1_out ? xor_1_out : 1'bz;  // Controlled_Buffer controlled_buffer_2
  assign controlled_buffer_3_out = not_1_out ? xor_2_out : 1'bz;  // Controlled_Buffer controlled_buffer_3
  assign controlled_buffer_4_out = not_1_out ? xor_3_out : 1'bz;  // Controlled_Buffer controlled_buffer_4
  not not_1 (not_1_out, and_5_out);
  D_Flip_Flop #(.trigger("falling")) d_ff_1 (
    .D(controlled_buffer_1_out), .clk(clock_1_out), .Q(d_ff_1_q[0]));  // open: Qn, preset, reset
  D_Flip_Flop #(.trigger("falling")) d_ff_2 (
    .D(controlled_buffer_2_out), .clk(clock_1_out), .Q(d_ff_1_q[1]));  // open: Qn, preset, reset
  D_Flip_Flop #(.trigger("falling")) d_ff_3 (
    .D(controlled_buffer_3_out), .clk(clock_1_out), .Q(d_ff_1_q[2]));  // open: Qn, preset, reset
  D_Flip_Flop #(.trigger("falling")) d_ff_4 (
    .D(controlled_buffer_4_out), .clk(clock_1_out), .Q(d_ff_1_q[3]));  // open: Qn, preset, reset
  assign controlled_buffer_1_out = and_5_out ? multiplexer_1_out[0] : 1'bz;  // Controlled_Buffer controlled_buffer_5
  assign controlled_buffer_2_out = and_5_out ? multiplexer_1_out[1] : 1'bz;  // Controlled_Buffer controlled_buffer_6
  assign controlled_buffer_3_out = and_5_out ? multiplexer_1_out[2] : 1'bz;  // Controlled_Buffer controlled_buffer_7
  assign controlled_buffer_4_out = and_5_out ? multiplexer_1_out[3] : 1'bz;  // Controlled_Buffer controlled_buffer_8
  Clock clock_1 (.out(clock_1_out));
  Decoder #(.select(2)) decoder_1 (
    .out0(controlled_buffer_19_out[3]), .out1(decoder_1_out1), .out2(decoder_1_out2), .out3(decoder_1_out3),
    .sel(multiplexer_1_out[7:6]), .en(clock_1_out));
  and and_5 (and_5_out, decoder_1_out3, d_ff_21_q);
  assign controlled_buffer_10_out[1] = controlled_buffer_19_out[3] ? multiplexer_1_out[5] : 1'bz;  // Controlled_Buffer controlled_buffer_9
  assign controlled_buffer_10_out[0] = controlled_buffer_19_out[3] ? multiplexer_1_out[4] : 1'bz;  // Controlled_Buffer controlled_buffer_10
  assign controlled_buffer_12_out[1] = controlled_buffer_19_out[3] ? multiplexer_1_out[3] : 1'bz;  // Controlled_Buffer controlled_buffer_11
  assign controlled_buffer_12_out[0] = controlled_buffer_19_out[3] ? multiplexer_1_out[2] : 1'bz;  // Controlled_Buffer controlled_buffer_12
  assign controlled_buffer_14_out[1] = controlled_buffer_19_out[3] ? multiplexer_1_out[1] : 1'bz;  // Controlled_Buffer controlled_buffer_13
  assign controlled_buffer_14_out[0] = controlled_buffer_19_out[3] ? multiplexer_1_out[0] : 1'bz;  // Controlled_Buffer controlled_buffer_14
  Decoder #(.select(2)) decoder_2 (
    .out0(decoder_2_out0[0]), .out1(decoder_2_out0[1]), .out2(decoder_2_out0[2]), .out3(decoder_2_out0[3]),
    .sel(multiplexer_1_out[5:4]), .en(decoder_1_out1));
  Decoder #(.select(2)) decoder_3 (
    .out0(decoder_3_out0), .out1(decoder_3_out1), .out2(decoder_3_out2), .out3(decoder_3_out3),
    .sel(multiplexer_1_out[5:4]), .en(decoder_1_out2));
  assign controlled_buffer_15_out = decoder_1_out1 ? multiplexer_1_out[0] : 1'bz;  // Controlled_Buffer controlled_buffer_15
  assign controlled_buffer_16_out = decoder_1_out1 ? multiplexer_1_out[1] : 1'bz;  // Controlled_Buffer controlled_buffer_16
  assign controlled_buffer_17_out = decoder_1_out1 ? multiplexer_1_out[2] : 1'bz;  // Controlled_Buffer controlled_buffer_17
  assign controlled_buffer_18_out = decoder_1_out1 ? multiplexer_1_out[3] : 1'bz;  // Controlled_Buffer controlled_buffer_18
  assign controlled_buffer_19_out = decoder_1_out1 ? decoder_2_out0 : 4'bz;  // Controlled_Buffer controlled_buffer_19
  Multiplexer #(.select(4), .width(8)) multiplexer_1 (
    .in0(in_1), .in1(in_3), .in2(in_4), .in3(in_5), .in4(in_6), .in5(in_7), .in6(in_8), .in7(in_9),
    .in8(in_10), .in9(in_11), .in10(in_12), .in11(in_13), .in12(in_14), .in13(in_15), .in14(in_16),
    .in15(in_17), .out(multiplexer_1_out), .sel(d_ff_1_q));
  Decoder #(.select(2)) decoder_4 (
    .out0(decoder_4_out0[0]), .out1(decoder_4_out0[1]), .out2(decoder_4_out0[2]), .out3(decoder_4_out0[3]),
    .sel(multiplexer_1_out[1:0]), .en(decoder_1_out2));
  assign controlled_buffer_19_out = decoder_1_out2 ? decoder_4_out0 : 4'bz;  // Controlled_Buffer controlled_buffer_20
  D_Flip_Flop d_ff_5 (
    .D(controlled_buffer_15_out), .clk(controlled_buffer_19_out[0]), .Q(d_ff_5_q[0]));  // open: Qn, preset, reset
  D_Flip_Flop d_ff_6 (
    .D(controlled_buffer_15_out), .clk(controlled_buffer_19_out[1]), .Q(d_ff_6_q[0]));  // open: Qn, preset, reset
  D_Flip_Flop d_ff_7 (
    .D(controlled_buffer_15_out), .clk(controlled_buffer_19_out[2]), .Q(d_ff_7_q[0]));  // open: Qn, preset, reset
  D_Flip_Flop #(.trigger("falling")) d_ff_8 (
    .D(controlled_buffer_15_out), .clk(controlled_buffer_19_out[3]), .Q(out_18[0]));  // open: Qn, preset, reset
  D_Flip_Flop d_ff_9 (
    .D(controlled_buffer_16_out), .clk(controlled_buffer_19_out[0]), .Q(d_ff_5_q[1]));  // open: Qn, preset, reset
  assign controlled_buffer_15_out = decoder_3_out0 ? d_ff_5_q[0] : 1'bz;  // Controlled_Buffer controlled_buffer_21
  D_Flip_Flop d_ff_10 (
    .D(controlled_buffer_16_out), .clk(controlled_buffer_19_out[1]), .Q(d_ff_6_q[1]));  // open: Qn, preset, reset
  assign controlled_buffer_15_out = decoder_3_out1 ? d_ff_6_q[0] : 1'bz;  // Controlled_Buffer controlled_buffer_22
  D_Flip_Flop d_ff_11 (
    .D(controlled_buffer_16_out), .clk(controlled_buffer_19_out[2]), .Q(d_ff_7_q[1]));  // open: Qn, preset, reset
  D_Flip_Flop #(.trigger("falling")) d_ff_12 (
    .D(controlled_buffer_16_out), .clk(controlled_buffer_19_out[3]), .Q(out_18[1]));  // open: Qn, preset, reset
  assign controlled_buffer_15_out = decoder_3_out3 ? out_18[0] : 1'bz;  // Controlled_Buffer controlled_buffer_23
  D_Flip_Flop d_ff_13 (
    .D(controlled_buffer_17_out), .clk(controlled_buffer_19_out[0]), .Q(d_ff_5_q[2]));  // open: Qn, preset, reset
  assign controlled_buffer_16_out = decoder_3_out0 ? d_ff_5_q[1] : 1'bz;  // Controlled_Buffer controlled_buffer_24
  D_Flip_Flop d_ff_14 (
    .D(controlled_buffer_17_out), .clk(controlled_buffer_19_out[1]), .Q(d_ff_6_q[2]));  // open: Qn, preset, reset
  assign controlled_buffer_16_out = decoder_3_out1 ? d_ff_6_q[1] : 1'bz;  // Controlled_Buffer controlled_buffer_25
  D_Flip_Flop d_ff_15 (
    .D(controlled_buffer_17_out), .clk(controlled_buffer_19_out[2]), .Q(d_ff_7_q[2]));  // open: Qn, preset, reset
  assign controlled_buffer_15_out = decoder_3_out2 ? d_ff_7_q[0] : 1'bz;  // Controlled_Buffer controlled_buffer_26
  D_Flip_Flop #(.trigger("falling")) d_ff_16 (
    .D(controlled_buffer_17_out), .clk(controlled_buffer_19_out[3]), .Q(out_18[2]));  // open: Qn, preset, reset
  assign controlled_buffer_16_out = decoder_3_out3 ? out_18[1] : 1'bz;  // Controlled_Buffer controlled_buffer_27
  D_Flip_Flop d_ff_17 (
    .D(controlled_buffer_18_out), .clk(controlled_buffer_19_out[0]), .Q(d_ff_5_q[3]));  // open: Qn, preset, reset
  assign controlled_buffer_17_out = decoder_3_out0 ? d_ff_5_q[2] : 1'bz;  // Controlled_Buffer controlled_buffer_28
  D_Flip_Flop d_ff_18 (
    .D(controlled_buffer_18_out), .clk(controlled_buffer_19_out[1]), .Q(d_ff_6_q[3]));  // open: Qn, preset, reset
  assign controlled_buffer_17_out = decoder_3_out1 ? d_ff_6_q[2] : 1'bz;  // Controlled_Buffer controlled_buffer_29
  D_Flip_Flop d_ff_19 (
    .D(controlled_buffer_18_out), .clk(controlled_buffer_19_out[2]), .Q(d_ff_7_q[3]));  // open: Qn, preset, reset
  assign controlled_buffer_16_out = decoder_3_out2 ? d_ff_7_q[1] : 1'bz;  // Controlled_Buffer controlled_buffer_30
  D_Flip_Flop #(.trigger("falling")) d_ff_20 (
    .D(controlled_buffer_18_out), .clk(controlled_buffer_19_out[3]), .Q(out_18[3]));  // open: Qn, preset, reset
  assign controlled_buffer_17_out = decoder_3_out3 ? out_18[2] : 1'bz;  // Controlled_Buffer controlled_buffer_31
  assign controlled_buffer_18_out = decoder_3_out0 ? d_ff_5_q[3] : 1'bz;  // Controlled_Buffer controlled_buffer_32
  assign controlled_buffer_18_out = decoder_3_out1 ? d_ff_6_q[3] : 1'bz;  // Controlled_Buffer controlled_buffer_33
  assign controlled_buffer_17_out = decoder_3_out2 ? d_ff_7_q[2] : 1'bz;  // Controlled_Buffer controlled_buffer_34
  assign controlled_buffer_18_out = decoder_3_out3 ? out_18[3] : 1'bz;  // Controlled_Buffer controlled_buffer_35
  assign controlled_buffer_18_out = decoder_3_out2 ? d_ff_7_q[3] : 1'bz;  // Controlled_Buffer controlled_buffer_36
  Multiplexer #(.select(2), .width(4)) multiplexer_2 (
    .in0(d_ff_5_q), .in1(d_ff_6_q), .in2(d_ff_7_q), .in3(out_18), .out(multiplexer_2_out),
    .sel(controlled_buffer_12_out));
  Multiplexer #(.select(2), .width(4)) multiplexer_3 (
    .in0(d_ff_5_q), .in1(d_ff_6_q), .in2(d_ff_7_q), .in3(out_18), .out(multiplexer_3_out),
    .sel(controlled_buffer_14_out));
  Adder #(.width(1)) adder_1 (
    .a(multiplexer_2_out[0]), .b(multiplexer_3_out[0]), .out(adder_1_out[0]), .cout(adder_1_cout));  // open: cin
  Adder #(.width(1)) adder_2 (
    .a(multiplexer_2_out[1]), .b(multiplexer_3_out[1]), .out(adder_1_out[1]), .cin(adder_1_cout),
    .cout(adder_2_cout));
  Subtractor #(.width(1)) subtractor_1 (
    .a(multiplexer_2_out[0]), .b(multiplexer_3_out[0]), .out(subtractor_1_out[0]), .bout(subtractor_1_bout));  // open: bin
  Subtractor #(.width(1)) subtractor_2 (
    .a(multiplexer_2_out[1]), .b(multiplexer_3_out[1]), .out(subtractor_1_out[1]), .bin(subtractor_1_bout),
    .bout(subtractor_2_bout));
  xor xor_5 (xor_5_out[0], multiplexer_2_out[0], multiplexer_3_out[0]);
  xor xor_6 (xor_5_out[1], multiplexer_2_out[1], multiplexer_3_out[1]);
  xor xor_7 (xor_5_out[2], multiplexer_2_out[2], multiplexer_3_out[2]);
  xor xor_8 (xor_5_out[3], multiplexer_2_out[3], multiplexer_3_out[3]);
  assign controlled_buffer_15_out = controlled_buffer_19_out[3] ? multiplexer_4_out[0] : 1'bz;  // Controlled_Buffer controlled_buffer_37
  assign controlled_buffer_16_out = controlled_buffer_19_out[3] ? multiplexer_4_out[1] : 1'bz;  // Controlled_Buffer controlled_buffer_38
  assign controlled_buffer_17_out = controlled_buffer_19_out[3] ? multiplexer_4_out[2] : 1'bz;  // Controlled_Buffer controlled_buffer_39
  assign controlled_buffer_18_out = controlled_buffer_19_out[3] ? multiplexer_4_out[3] : 1'bz;  // Controlled_Buffer controlled_buffer_40
  Adder #(.width(1)) adder_3 (
    .a(multiplexer_2_out[2]), .b(multiplexer_3_out[2]), .out(adder_1_out[2]), .cin(adder_2_cout),
    .cout(adder_3_cout));
  Adder #(.width(1)) adder_4 (
    .a(multiplexer_2_out[3]), .b(multiplexer_3_out[3]), .out(adder_1_out[3]), .cin(adder_3_cout));  // open: cout
  Subtractor #(.width(1)) subtractor_3 (
    .a(multiplexer_2_out[2]), .b(multiplexer_3_out[2]), .out(subtractor_1_out[2]), .bin(subtractor_2_bout),
    .bout(subtractor_3_bout));
  Subtractor #(.width(1)) subtractor_4 (
    .a(multiplexer_2_out[3]), .b(multiplexer_3_out[3]), .out(subtractor_1_out[3]), .bin(subtractor_3_bout));  // open: bout
  and and_6 (and_6_out[0], multiplexer_2_out[0], multiplexer_3_out[0]);
  and and_7 (and_6_out[1], multiplexer_2_out[1], multiplexer_3_out[1]);
  and and_8 (and_6_out[2], multiplexer_2_out[2], multiplexer_3_out[2]);
  and and_9 (and_6_out[3], multiplexer_2_out[3], multiplexer_3_out[3]);
  Multiplexer #(.enable("true"), .select(2), .width(4)) multiplexer_4 (
    .in0(adder_1_out), .in1(subtractor_1_out), .in2(and_6_out), .in3(xor_5_out), .out(multiplexer_4_out),
    .sel(controlled_buffer_10_out));  // open: en
  nor nor_1 (nor_1_out, multiplexer_4_out[0], multiplexer_4_out[1], multiplexer_4_out[2], multiplexer_4_out[3]);
  D_Flip_Flop #(.trigger("high")) d_ff_21 (
    .D(controlled_inverter_1_out), .clk(controlled_buffer_19_out[3]), .Q(d_ff_21_q));  // open: Qn, preset, reset
  assign controlled_inverter_1_out = controlled_buffer_19_out[3] ? ~nor_1_out : 1'bz;  // Controlled_Inverter controlled_inverter_1

  // Notes on the sheet:
  //   Instructie register 
  //   PC
  //   1
  //   2
  //   ALU
endmodule
